# Fritzing sketch Phone Clicker (saved by Fritzing 0.9.3b)

parts:
  Stepper_Driver = 28BYJ-48 Driver Module [part_number=ULN2003 package=THT]
  Stepper = 28BYJ-48 Stepper Motor [part_number=28BYJ-48]
  Arduino_Uno = Arduino Uno (Rev3)

nets:
  N1: Stepper_Driver.IN1, Arduino_Uno.D4
  N2: Stepper_Driver.IN2, Arduino_Uno.D5_PWM
  N3: Stepper_Driver.IN3, Arduino_Uno.D6_PWM
  N4: Stepper_Driver.IN4, Arduino_Uno.D7
  GND: Stepper_Driver.GND, Arduino_Uno.GND
  N5: Stepper_Driver.Vmotor, Arduino_Uno.5V
  N6: Stepper_Driver.blue-pin, Stepper.blue-pin
  N7: Stepper_Driver.pink-pin, Stepper.pink-pin
  N8: Stepper_Driver.yellow-pin, Stepper.yellow-pin
  N9: Stepper_Driver.orange-pin, Stepper.orange-pin
  N10: Stepper_Driver.red-pin, Stepper.red-pin

custom parts:
  28BYJ-48 Driver Module: Generic male header
  28BYJ-48 Stepper Motor: Unipolar Stepper Motor 28BYJ-48 Top coil - pink & orange Bottom coil - blue & yellow Common rail - red Connector pins: blue - pink - yellow - orange - red

// code stored in the sketch: Zeke.ino
#include <AccelStepper.h>



#define stepperPin1  4     // IN1 on the ULN2003 driver
#define stepperPin2  5     // IN2 on the ULN2003 driver
#define stepperPin3  6     // IN3 on the ULN2003 driver
#define stepperPin4  7     // IN4 on the ULN2003 driver



#define MotorInterfaceType 8  // Define the AccelStepper interface type; 4 wire motor in half step mode


/* Adujust These
---------------------------*/
int delayTime = 1000;
int steps = 1400;
int stepperSpeed = 1000; // I would leave this where it is at
/*-------------------------
       Adjust These*/


bool on = false;


AccelStepper stepper = AccelStepper(MotorInterfaceType, stepperPin1, stepperPin3, stepperPin2, stepperPin4);


void setup() {
  Serial.begin(9600);


  stepper.setMaxSpeed(1000);
  stepper.setCurrentPosition(0);
}


void loop() {
if (Serial.available() > 0) {
  int state = Serial.read();


  if (state == 'A' || state == 'a') {
    on = true;
  }


  if (state == 'B' || state == 'b') {
    stepper.move(100); 


    stepper.setSpeed(stepperSpeed);
    while (stepper.currentPosition() != stepper.targetPosition()) {
     stepper.runSpeedToPosition();
    }
   }
    
  if (state == 'C' || state == 'c') {
    stepper.move(-100); 


    stepper.setSpeed(-stepperSpeed);
    while (stepper.currentPosition() != stepper.targetPosition()) {
      stepper.runSpeedToPosition();
    }
  }


  while (on == true) {
    click();
  }
}// Serial Avalible
}// Loop


void click() {


  delay(delayTime);


  stepper.move(steps); 


  stepper.setSpeed(stepperSpeed);
  while (stepper.currentPosition() != stepper.targetPosition()) {
    stepper.runSpeedToPosition();
  }
  stepper.move(-steps);


  stepper.setSpeed(-stepperSpeed);
  while  (stepper.currentPosition() != stepper.targetPosition()) {
    stepper.runSpeedToPosition();
  }
}// Click
